# Fritzing sketch digital-input-button_Button (saved by Fritzing 0.8.3b)
circuit board: 2.92478cm x 5.58617cm
breadboards: 1

parts:
  +_- = mystery part, 2 pins [chip_label=PWR-IN]
  o_i = mystery part, 2 pins [chip_label=DATA-IN]
  +_-_2 = mystery part, 2 pins [chip_label=PWR-OUT]
  i_o = mystery part, 2 pins [chip_label=DATA-OUT]
  R1 = Resistor [tolerance=±5% resistance=10k package="0805 [SMD]"]
  R2 = Resistor [tolerance=±5% resistance=220 package="0805 [SMD]"]
  Power = smd LED [color="Blue (505nm)" package="0805 [SMD]"]
  U1 = mystery part, 1 pin [chip_label=?]
  U2 = mystery part, 1 pin [chip_label=?]
  J1 = female pin header, 1 pin [form="♀ (female)"]  # not connected
  J2 = female pin header, 1 pin [form="♀ (female)"]  # not connected

nets:
  N1: +_-.pin1, +_-_2.pin2, R1.Pin_1, Power.cathode
  N2: +_-.pin2, +_-_2.pin1, R2.Pin_0, U1.pin1
  N3: o_i.pin1, i_o.pin1, R1.Pin_0, U2.pin1
  N4: o_i.pin2, i_o.pin2
  N5: R2.Pin_1, Power.anode

notes:
  In this example, a pushbutton is used as a digital input and an LED is a digital output. Related example: http://arduino.cc/en/Tutorial/Button
