# Fritzing sketch digital-temp-LM75A (saved by Fritzing 0.8.0b)
breadboards: 1

parts:
  +_- = mystery part, 2 pins [chip_label=PWR-IN]
  d_c = mystery part, 2 pins [chip_label=DATA-IN]
  +_-_2 = mystery part, 2 pins [chip_label=PWR-OUT]
  c_d = mystery part, 2 pins [chip_label=DATA-OUT]
  R2 = Resistor [tolerance=±5% resistance=10k package="0805 [SMD]"]
  PWR = smd LED [color="Red (633nm)" package="0805 [SMD]"]
  TEMP_SENSOR = SO08 [chip_label=IC package=SO]
  C1 = Tantalum Capacitor [capacitance="1 μF" package="A 3216 [SMD, tantalum]"]

nets:
  N1: +_-.pin1, +_-_2.pin2, PWR.cathode, TEMP_SENSOR.4, TEMP_SENSOR.7, C1.-
  N2: +_-.pin2, +_-_2.pin1, R2.Pin_1, TEMP_SENSOR.8, C1.+
  N3: d_c.pin1, c_d.pin2, TEMP_SENSOR.1
  N4: d_c.pin2, c_d.pin1, TEMP_SENSOR.2
  N5: R2.Pin_0, PWR.anode

notes:
  In this example, a pushbutton is used as a digital input and an LED is a digital output. Related example: http://arduino.cc/en/Tutorial/Button
