# Fritzing sketch Display-I2C-8x2LCD (saved by Fritzing 0.8.0b)
breadboards: 1

parts:
  J2 = female pin header, 5 pins [form="♀ (female)"]
  I2C_LCD_Adaptor = LCD screen
  R1 = Trimmer Potentiometer [maximum_resistance=10kΩ package=THT]
  MCP9808 = MCP9808-SSOP20 [part_number=MCP9808-E/SS chip_label=IC package=SSOP20]
  Pad1 = Pad [width=1.61270647619049 height=0.56444565396826 connect=center]
  Pad2 = Pad [width=1.61270647619049 height=0.56444565396826 connect=center]  # not connected
  Pad3 = Pad [width=1.61270647619049 height=0.56444565396826 connect=center]
  Pad4 = Pad [width=1.61270647619049 height=0.56444565396826 connect=center]
  Pad5 = Pad [width=1.61270647619049 height=0.56444565396826 connect=center]
  Pad6 = Pad [width=1.61270647619049 height=0.56444565396826 connect=center]
  Pad7 = Pad [width=1.61270647619049 height=0.56444565396826 connect=center]  # not connected
  Pad8 = Pad [width=1.61270647619049 height=0.56444565396826 connect=center]  # not connected
  Pad9 = Pad [width=1.61270647619049 height=0.56444565396826 connect=center]
  J3 = female pin header, 2 pins [form="♀ (female)"]  # not connected
  J4 = female pin header, 2 pins [form="♀ (female)"]  # not connected

nets:
  VSS: J2.pin1, I2C_LCD_Adaptor.VSS, I2C_LCD_Adaptor.R/W, I2C_LCD_Adaptor.LED-, R1.leg2, MCP9808.A0, MCP9808.VSS, Pad3.pad, Pad6.pad
  VDD: J2.pin2, I2C_LCD_Adaptor.VDD, I2C_LCD_Adaptor.LED+, R1.leg1, MCP9808.RESET, MCP9808.VCC, Pad9.pad
  N1: J2.pin3, MCP9808.INT
  N2: J2.pin4, MCP9808.SDA
  N3: J2.pin5, MCP9808.SCL
  N4: I2C_LCD_Adaptor.V0, R1.wiper
  N5: I2C_LCD_Adaptor.RS, MCP9808.GP5
  N6: I2C_LCD_Adaptor.E, MCP9808.GP4
  N7: I2C_LCD_Adaptor.DB4, MCP9808.GP0
  N8: I2C_LCD_Adaptor.DB5, MCP9808.GP1
  N9: I2C_LCD_Adaptor.DB6, MCP9808.GP2
  N10: I2C_LCD_Adaptor.DB7, MCP9808.GP3
  N11: MCP9808.A2, Pad1.pad, Pad4.pad
  N12: MCP9808.A1, Pad5.pad

notes:
  Clixx.io
  - + i d c
