# Fritzing sketch Power-ButtonBattery (saved by Fritzing 0.8.0b)
breadboards: 1

parts:
  o_i = female pin header, 2 pins [form="♀ (female)"]
  + = Pad [width=1 height=3 connect=center]
  - = Pad [width=1 height=3 connect=center]
  i = Pad [width=1 height=3 connect=center]  # not connected
  +_- = female pin header, 2 pins [form="♀ (female)"]
  o = Pad [width=1 height=3 connect=center]
  R1 = Resistor [tolerance=±5% resistance=220 package="0805 [SMD]"]
  +_2 = Pad [width=2.4913322375479 height=5.87802031417625 connect=center]
  -_2 = Pad [width=2.53028182375479 height=7.47402688122605 connect=center]

nets:
  N1: o_i.pin1, o.pad, R1.Pin_0
  GND: o_i.pin2, -.pad, +_-.pin2, -_2.pad
  N2: +.pad, +_-.pin1, R1.Pin_1, +_2.pad

notes:
  r0.1
  Coin Cell
