# Fritzing sketch power-variable-lm317 (saved by Fritzing 0.8.0b)
breadboards: 1

parts:
  i_o = female pin header, 2 pins [form="♀ (female)"]
  Power = SO08 [chip_label=IC package=SO]
  + = Pad [width=1 height=3 connect=center]  # not connected
  - = Pad [width=1 height=3 connect=center]  # not connected
  i = Pad [width=1 height=3 connect=center]  # not connected
  +_- = female pin header, 2 pins [form="♀ (female)"]
  +_-_2 = female pin header, 2 pins [form="♀ (female)"]
  i_o_2 = female pin header, 2 pins [form="♀ (female)"]
  R1 = Resistor [tolerance=±5% resistance=220 package="0805 [SMD]"]
  Adjust = Trimmer Potentiometer [maximum_resistance=10kΩ package=THT]
  o = Pad [width=1 height=3 connect=center]  # not connected

nets:
  N1: i_o.pin1, i_o_2.pin1
  N2: i_o.pin2, i_o_2.pin2
  N3: Power.1, +_-_2.pin1
  N4: Power.2, Power.3, Power.6, Power.7, +_-.pin1, R1.Pin_0
  N5: Power.4, R1.Pin_1, Adjust.leg2
  GND: +_-.pin2, +_-_2.pin2, Adjust.leg1

notes:
  << Input
  r0.2
  << Output
