# Fritzing sketch power-mosfet-n (saved by Fritzing 0.8.0b)
breadboards: 1

parts:
  i_o = female pin header, 2 pins [form="♀ (female)"]
  + = Pad [width=1 height=3 connect=center]  # not connected
  - = Pad [width=1 height=3 connect=center]  # not connected
  i = Pad [width=1 height=3 connect=center]  # not connected
  +_- = female pin header, 2 pins [form="♀ (female)"]
  +_-_2 = female pin header, 2 pins [form="♀ (female)"]
  i_o_2 = female pin header, 2 pins [form="♀ (female)"]
  R1 = Resistor [tolerance=±5% resistance=220 package="0805 [SMD]"]
  o = Pad [width=1 height=3 connect=center]  # not connected
  Q1 = Basic FET N-Channel [package="TO220 [THT]"]
  J1 = female pin header, 1 pin [form="♀ (female)"]
  J1_2 = female pin header, 1 pin [form="♀ (female)"]

nets:
  N1: i_o.pin1, R1.Pin_1, Q1.gate
  N2: i_o.pin2, i_o_2.pin1
  N3: +_-.pin1, +_-_2.pin1
  GND: +_-.pin2, R1.Pin_0, Q1.source
  N4: +_-_2.pin2, i_o_2.pin2, J1.pin1
  N5: Q1.drain, J1_2.pin1

notes:
  << Input
  r0.2
  << Output
