# Fritzing sketch power-voltmeter (saved by Fritzing 0.7.12b)
breadboards: 1

parts:
  o_i = female pin header, 2 pins [form="♀ (female)"]
  + = Pad [width=1 height=3 connect=center]
  - = Pad [width=1 height=3 connect=center]
  i = Pad [width=1 height=3 connect=center]
  +_- = female pin header, 2 pins [form="♀ (female)"]
  o = Pad [width=1 height=3 connect=center]
  J1 = female pin header, 3 pins [form="♀ (female)"]
  S1 = Toggle Switch [package=THT]

nets:
  N1: o_i.pin1, i.pad
  N2: o_i.pin2, o.pad, S1.L1
  N3: +.pad, +_-.pin1, J1.pin2, S1.L2
  GND: -.pad, +_-.pin2, J1.pin3
  N4: J1.pin1, S1.COM

notes:
  r0.2
  Voltmeter
