# Fritzing sketch radio-i2c-tea5767 (saved by Fritzing 0.8.0b)
breadboards: 1

parts:
  i_o = female pin header, 2 pins [form="♀ (female)"]  # not connected
  + = Pad [width=1 height=3 connect=center]  # not connected
  - = Pad [width=1 height=3 connect=center]  # not connected
  i = Pad [width=1 height=3 connect=center]  # not connected
  +_- = female pin header, 2 pins [form="♀ (female)"]
  +_-_2 = female pin header, 2 pins [form="♀ (female)"]
  i_o_2 = female pin header, 2 pins [form="♀ (female)"]  # not connected
  o = Pad [width=1 height=3 connect=center]  # not connected
  J2 = female pin header, 4 pins [form="♀ (female)"]  # not connected
  J3 = female pin header, 4 pins [form="♀ (female)"]  # not connected
  Antenae = female pin header, 1 pin [form="♀ (female)"]  # not connected

nets:
  N1: +_-.pin1, +_-_2.pin1
  GND: +_-.pin2

notes:
  << Input
  r0.2
  << Output
